# Fritzing sketch hipphapp (saved by Fritzing 0.9.3b)
breadboards: 1

parts:
  S1 = Pushbutton [package="[THT]"]
  LED1 = smd LED [color="Yellow (585nm)" package="0603 [SMD]"]
  R1 = Resistor [tolerance=±5% resistance=220 package="0603 [SMD]"]
  Part1 = Arduino Uno (Rev3)

nets:
  N1: S1.Pin_1, S1.Pin_2, LED1.cathode, Part1.GND
  N2: S1.Pin_3, S1.Pin_4, Part1.D3_PWM
  N3: LED1.anode, R1.Pin_0
  N4: R1.Pin_1, Part1.D6_PWM
